// Logisim project Cse315P.circ as structural Verilog: 13 circuits, main circuit main
module main (
  output [17:0] out_1,
  output out_2
);

  wire button_1_out, button_2_out, button_3_out, clock_1_out;

  Button button_1 (.out(button_1_out));
  Button button_2 (.out(button_2_out));
  Button button_3 (.out(button_3_out));
  Clock clock_1 (.out(clock_1_out));
  CPU cpu_1 (
    .clock(clock_1_out), .Carry_Out(out_2), .in_4(button_3_out), .in_3(button_2_out), .in_2(button_1_out),
    .out_5(out_1));
endmodule

module Control_Unit (
  input  [17:0] Instruction,
  input  [17:0] SRC1_Value,
  input  [17:0] SRC2_Value,
  input  Clock,
  output Compare,
  output Imm_Signal,
  output [13:0] ADDR,
  output Jump,
  output [3:0] DR,
  output [3:0] SR1,
  output [3:0] SR2,
  output Branch_Signal,
  output [1:0] ALU_Option,
  output [13:0] Address14,
  output [13:0] LD_ST_ADDR,
  output [3:0] SRC1,
  output [3:0] SRC2,
  output [17:0] Imm,
  output Mem_Load,
  output Store,
  output PC_Read,
  output INST_Read,
  output Register_Write,
  output Mem_Store
);

  wire ADD, ADDI, AND, and_1_out, and_2_out, and_4_out, and_5_out, and_6_out, and_7_out, and_8_out,
       and_9_out, and_10_out, and_11_out, ANDI, BEQ, BGE, BGT, BLE, BLT, JUMP_t, LD, n18_bit_comparator_1_eq,
       n18_bit_comparator_1_gt, n18_bit_comparator_1_lt, OR, or_1_out, or_5_out, or_7_out, or_8_out,
       or_9_out, ORI, Reset, State3, State4, State5, XOR, XORI;
  wire [2:0] counter_1_q;

  Decoder #(.select(4)) decoder_1 (
    .out0(AND), .out1(ANDI), .out2(ADD), .out3(ADDI), .out4(OR), .out5(ORI), .out6(XOR), .out7(XORI),
    .out8(LD), .out9(Mem_Store), .out10(JUMP_t), .out11(BEQ), .out12(BGT), .out13(BLT), .out14(BGE),
    .out15(BLE), .sel(Instruction[17:14]));  // open: en
  Counter #(.width(3), .max('h4)) counter_1 (.Q(counter_1_q), .clk(Clock), .clr(Reset));  // open: load, D, count, carry
  assign ADDR = {{8{1'b0}}, Instruction[5:0]};  // Bit_Extender bit_extender_1
  assign Imm = {{12{Instruction[5]}}, Instruction[5:0]};  // Bit_Extender bit_extender_2
  // Probe on Reset
  Decoder #(.select(3), .enable("false")) decoder_2 (
    .out0(PC_Read), .out1(INST_Read), .out2(State3), .out3(State4), .out4(State5), .sel(counter_1_q));  // open: out5, out6, out7
  or or_1 (or_1_out, AND, ANDI, ADD, ADDI, OR, ORI, XOR, XORI);
  and and_1 (and_1_out, State3, or_1_out);
  and and_2 (and_2_out, State4, LD);
  assign LD_ST_ADDR = {{4{1'b0}}, Instruction[9:0]};  // Bit_Extender bit_extender_3
  and and_3 (Mem_Load, State3, LD);
  or or_2 (Register_Write, and_1_out, and_2_out);
  or or_3 (Imm_Signal, ANDI, ADDI, ORI, XORI);
  or or_4 (Compare, BEQ, BGT, BLT, BGE, BLE);
  and and_4 (and_4_out, State5, LD);
  or or_5 (or_5_out, AND, ANDI, ADD, ADDI, OR, ORI, XOR, XORI, Mem_Store, JUMP_t, BEQ, BGT, BLT, BGE, BLE);
  and and_5 (and_5_out, State4, or_5_out);
  or or_6 (Reset, and_4_out, and_5_out);
  _18_Bit_Comparator u_18_bit_comparator_1 (
    .EQ(n18_bit_comparator_1_eq), .GT(n18_bit_comparator_1_gt), .LT(n18_bit_comparator_1_lt), .A(SRC1_Value),
    .B(SRC2_Value));
  or or_7 (or_7_out, n18_bit_comparator_1_eq, n18_bit_comparator_1_gt);
  or or_8 (or_8_out, n18_bit_comparator_1_eq, n18_bit_comparator_1_gt);
  and and_6 (and_6_out, BEQ, n18_bit_comparator_1_eq);
  and and_7 (and_7_out, n18_bit_comparator_1_gt, BGT);
  and and_8 (and_8_out, n18_bit_comparator_1_lt, BLT);
  and and_9 (and_9_out, or_7_out, BGE);
  and and_10 (and_10_out, or_8_out, BLE);
  or or_9 (or_9_out, BEQ, BGT, BLT, BGE, BLE);
  and and_11 (and_11_out, or_9_out, Branch_Signal);
  or or_10 (Branch_Signal, and_6_out, and_7_out, and_8_out, and_9_out, and_10_out);
  or or_11 (Jump, JUMP_t, and_11_out);

  assign Address14 = Instruction[13:0];
  assign ALU_Option = Instruction[16:15];
  assign DR = Instruction[13:10];
  assign SR1 = Instruction[9:6];
  assign SR2 = Instruction[3:0];
  assign SRC1 = Instruction[13:10];
  assign SRC2 = Instruction[9:6];
  assign Store = Mem_Store;

  // Other names for the same wires on the sheet: ST = Mem_Store; State1 = PC_Read; State2 = INST_Read
endmodule

module PC_Register (
  input  [13:0] JUMP_ADDRESS,
  input  ADDRSelect,
  input  Clear,
  input  Enable,
  input  Clock,
  input  BranchSignal,
  output [13:0] PC_address
);

  wire [13:0] multiplexer_1_out, multiplexer_2_out, n14_bit_adder_1_inst_read;

  Multiplexer #(.width(14)) multiplexer_1 (
    .in0(14'h1), .in1(JUMP_ADDRESS), .out(multiplexer_1_out), .sel(ADDRSelect));  // open: en
  _14_Bit_Adder u_14_bit_adder_1 (
    .INST_Read(n14_bit_adder_1_inst_read), .A(multiplexer_1_out), .B(multiplexer_2_out));  // open: c_out
  Multiplexer #(.width(14)) multiplexer_2 (
    .in0(PC_address), .in1({14{1'b0}}), .out(multiplexer_2_out), .sel(BranchSignal));  // open: en
  Register #(.width(14), .trigger("falling")) register_1 (
    .D(n14_bit_adder_1_inst_read), .en(Enable), .Q(PC_address), .clk(Clock), .clr(Clear));
endmodule

module Register_File (
  input  [3:0] Read_Register_1,
  input  [3:0] Read_Register_2,
  input  [3:0] Write_Register,
  input  [17:0] Input,
  input  reset,
  input  Register_Write,
  input  Clock,
  output [17:0] Read_Data_1,
  output [17:0] Register_Data_2
);

  wire and_1_out, and_2_out, and_3_out, and_4_out, and_5_out, and_6_out, and_7_out, and_8_out, and_9_out,
       and_10_out, and_11_out, and_12_out, and_13_out, and_14_out, and_15_out, and_16_out, decoder_1_out0,
       decoder_1_out1, decoder_1_out2, decoder_1_out3, decoder_1_out4, decoder_1_out5, decoder_1_out6,
       decoder_1_out7, decoder_1_out8, decoder_1_out9, decoder_1_out10, decoder_1_out11, decoder_1_out12,
       decoder_1_out13, decoder_1_out14, decoder_1_out15;
  wire [17:0] register_1_q, register_2_q, register_3_q, register_4_q, register_5_q, register_6_q,
       register_7_q, register_8_q, register_9_q, register_10_q, register_11_q, register_12_q, register_13_q,
       register_14_q, register_15_q, register_16_q;

  Decoder #(.select(4)) decoder_1 (
    .out0(decoder_1_out0), .out1(decoder_1_out1), .out2(decoder_1_out2), .out3(decoder_1_out3),
    .out4(decoder_1_out4), .out5(decoder_1_out5), .out6(decoder_1_out6), .out7(decoder_1_out7),
    .out8(decoder_1_out8), .out9(decoder_1_out9), .out10(decoder_1_out10), .out11(decoder_1_out11),
    .out12(decoder_1_out12), .out13(decoder_1_out13), .out14(decoder_1_out14), .out15(decoder_1_out15),
    .sel(Write_Register));  // open: en
  and and_1 (and_1_out, decoder_1_out0, Register_Write);
  and and_2 (and_2_out, decoder_1_out1, Register_Write);
  and and_3 (and_3_out, decoder_1_out2, Register_Write);
  and and_4 (and_4_out, decoder_1_out3, Register_Write);
  and and_5 (and_5_out, decoder_1_out4, Register_Write);
  and and_6 (and_6_out, decoder_1_out5, Register_Write);
  and and_7 (and_7_out, decoder_1_out6, Register_Write);
  and and_8 (and_8_out, decoder_1_out7, Register_Write);
  Register #(.width(18)) register_1 (.D(Input), .en(and_1_out), .Q(register_1_q), .clk(Clock), .clr(reset));
  Register #(.width(18)) register_2 (.D(Input), .en(and_2_out), .Q(register_2_q), .clk(Clock), .clr(reset));
  Register #(.width(18)) register_3 (.D(Input), .en(and_3_out), .Q(register_3_q), .clk(Clock), .clr(reset));
  Register #(.width(18)) register_4 (.D(Input), .en(and_4_out), .Q(register_4_q), .clk(Clock), .clr(reset));
  Register #(.width(18)) register_5 (.D(Input), .en(and_5_out), .Q(register_5_q), .clk(Clock), .clr(reset));
  Register #(.width(18)) register_6 (.D(Input), .en(and_6_out), .Q(register_6_q), .clk(Clock), .clr(reset));
  Register #(.width(18)) register_7 (.D(Input), .en(and_7_out), .Q(register_7_q), .clk(Clock), .clr(reset));
  Register #(.width(18)) register_8 (.D(Input), .en(and_8_out), .Q(register_8_q), .clk(Clock), .clr(reset));
  and and_9 (and_9_out, decoder_1_out8, Register_Write);
  and and_10 (and_10_out, decoder_1_out9, Register_Write);
  and and_11 (and_11_out, decoder_1_out10, Register_Write);
  and and_12 (and_12_out, decoder_1_out11, Register_Write);
  and and_13 (and_13_out, decoder_1_out12, Register_Write);
  and and_14 (and_14_out, decoder_1_out13, Register_Write);
  and and_15 (and_15_out, decoder_1_out14, Register_Write);
  and and_16 (and_16_out, decoder_1_out15, Register_Write);
  Register #(.width(18)) register_9 (.D(Input), .en(and_9_out), .Q(register_9_q), .clk(Clock), .clr(reset));
  Register #(.width(18)) register_10 (.D(Input), .en(and_10_out), .Q(register_10_q), .clk(Clock), .clr(reset));
  Register #(.width(18)) register_11 (.D(Input), .en(and_11_out), .Q(register_11_q), .clk(Clock), .clr(reset));
  Register #(.width(18)) register_12 (.D(Input), .en(and_12_out), .Q(register_12_q), .clk(Clock), .clr(reset));
  Register #(.width(18)) register_13 (.D(Input), .en(and_13_out), .Q(register_13_q), .clk(Clock), .clr(reset));
  Register #(.width(18)) register_14 (.D(Input), .en(and_14_out), .Q(register_14_q), .clk(Clock), .clr(reset));
  Register #(.width(18)) register_15 (.D(Input), .en(and_15_out), .Q(register_15_q), .clk(Clock), .clr(reset));
  Register #(.width(18)) register_16 (.D(Input), .en(and_16_out), .Q(register_16_q), .clk(Clock), .clr(reset));
  Multiplexer #(.select(4), .width(18)) multiplexer_1 (
    .in0(register_1_q), .in1(register_2_q), .in2(register_3_q), .in3(register_4_q), .in4(register_5_q),
    .in5(register_6_q), .in6(register_7_q), .in7(register_8_q), .in8(register_9_q), .in9(register_10_q),
    .in10(register_11_q), .in11(register_12_q), .in12(register_13_q), .in13(register_14_q),
    .in14(register_15_q), .in15(register_16_q), .out(Read_Data_1), .sel(Read_Register_1));  // open: en
  Multiplexer #(.select(4), .width(18)) multiplexer_2 (
    .in0(register_1_q), .in1(register_2_q), .in2(register_3_q), .in3(register_4_q), .in4(register_5_q),
    .in5(register_6_q), .in6(register_7_q), .in7(register_8_q), .in8(register_9_q), .in9(register_10_q),
    .in10(register_11_q), .in11(register_12_q), .in12(register_13_q), .in13(register_14_q),
    .in14(register_15_q), .in15(register_16_q), .out(Register_Data_2), .sel(Read_Register_2));  // open: en
endmodule

module CPU (
  input  clock,
  input  in_2,
  input  in_3,
  input  in_4,
  output [17:0] out_5,
  output Carry_Out
);

  wire Branch, Compare, Imm_Signal, inst_read, JUMPSig, Mem_Load, Mem_Store, not_1_out, PCRead,
       Register_Write;
  wire [1:0] ALU_Control;
  wire [3:0] Dest, multiplexer_3_out, multiplexer_4_out, multiplexer_5_out, SR1, SR2, SRC1, SRC2;
  wire [13:0] ADDR, JUMP_ADDR, LD_ST_ADDR, multiplexer_1_out, pc_register_1_pc_address;
  wire [17:0] ALU_Result, DataMemVal, Imm, multiplexer_2_out, multiplexer_6_out, REG1_Out, REG2_Out,
       register_file_1_read_data_1, register_file_1_register_data_2, rom_1_data, SRC1_Value, SRC2_Value;

  // Probe on multiplexer_1_out
  Multiplexer #(.width(14), .enable("false")) multiplexer_1 (
    .in0(JUMP_ADDR), .in1(ADDR), .out(multiplexer_1_out), .sel(Branch));
  // Probe on LD_ST_ADDR
  PC_Register pc_register_1 (
    .JUMP_ADDRESS(multiplexer_1_out), .ADDRSelect(JUMPSig), .PC_address(pc_register_1_pc_address),
    .Enable(PCRead), .Clock(clock), .Clear(in_4), .BranchSignal(Branch));
  // Probe on REG1_Out
  // Probe on multiplexer_1_out
  RAM #(.addrWidth(14), .dataWidth(18), .bus("separate")) ram_1 (
    .addr(LD_ST_ADDR), .din(REG1_Out), .data(DataMemVal), .str(Mem_Store), .clk(clock), .ld(Mem_Load));  // open: sel, clr
  Control_Unit control_unit_1 (
    .Instruction(out_5), .Clock(clock), .DR(Dest), .SR1(SR1), .Imm(Imm), .SR2(SR2), .LD_ST_ADDR(LD_ST_ADDR),
    .SRC1(SRC1), .SRC2(SRC2), .Imm_Signal(Imm_Signal), .Branch_Signal(Branch), .Store(Mem_Store),
    .Jump(JUMPSig), .PC_Read(PCRead), .INST_Read(inst_read), .Address14(JUMP_ADDR), .ALU_Option(ALU_Control),
    .Mem_Load(Mem_Load), .Mem_Store(Mem_Store), .SRC1_Value(SRC1_Value), .SRC2_Value(SRC2_Value),
    .ADDR(ADDR), .Compare(Compare), .Register_Write(Register_Write));
  // Probe on pc_register_1_pc_address
  // Probe on DataMemVal
  // Probe on rom_1_data
  ROM #(.addrWidth(14), .dataWidth(18)) rom_1 (.addr(pc_register_1_pc_address), .data(rom_1_data));  // open: sel
  not not_1 (not_1_out, Mem_Load);
  Register #(.width(18)) Instruction_Register (.D(rom_1_data), .en(inst_read), .Q(out_5), .clk(clock), .clr(in_3));
  // Probe on multiplexer_2_out
  Multiplexer #(.width(18)) multiplexer_2 (
    .in0(DataMemVal), .in1(ALU_Result), .out(multiplexer_2_out), .sel(not_1_out));  // open: en
  Multiplexer #(.width(4)) multiplexer_3 (.in0(SR1), .in1(SRC1), .out(multiplexer_3_out), .sel(Branch));  // open: en
  Multiplexer #(.width(4)) multiplexer_4 (.in0(SR2), .in1(SRC2), .out(multiplexer_4_out), .sel(Branch));  // open: en
  // Probe on multiplexer_4_out
  Multiplexer #(.width(4)) multiplexer_5 (
    .in0(multiplexer_3_out), .in1(Dest), .out(multiplexer_5_out), .sel(Mem_Store));  // open: en
  Register_File register_file_1 (
    .Read_Register_1(multiplexer_5_out), .Read_Register_2(multiplexer_4_out), .Write_Register(Dest),
    .Input(multiplexer_2_out), .Register_Write(Register_Write), .Clock(clock),
    .Read_Data_1(register_file_1_read_data_1), .Register_Data_2(register_file_1_register_data_2), .reset(in_2));
  // Probe on REG1_Out
  Multiplexer #(.width(18)) multiplexer_6 (
    .in0(REG2_Out), .in1(Imm), .out(multiplexer_6_out), .sel(Imm_Signal));  // open: en
  // Probe on multiplexer_6_out
  // Probe on ALU_Control
  Demultiplexer #(.width(18)) demultiplexer_1 (
    .out0(REG1_Out), .out1(SRC1_Value), .in(register_file_1_read_data_1), .sel(Compare));  // open: en
  Demultiplexer #(.width(18)) demultiplexer_2 (
    .out0(REG2_Out), .out1(SRC2_Value), .in(register_file_1_register_data_2), .sel(Compare));  // open: en
  // Probe on REG1_Out
  _18_Bit_ALU u_18_bit_alu_1 (
    .Input1(REG1_Out), .Input2(multiplexer_6_out), .Operation(ALU_Control), .Result(ALU_Result),
    .Carry_Out(Carry_Out));
  // Probe on SRC2_Value
  // Probe on ALU_Result
  // Probe on SRC1_Value
  // Probe on REG2_Out

  // Other names for the same wires on the sheet: Instruction[17:0] = out_5

  // Notes on the sheet:
  //   contents of rom_1 (hex, n*v repeats v):
  //   8042 c401 c081 2400a 20c0a 2c040 840 28002 9405 9400 5c45 12840 16c7c 1a043 1e47f 3bbde 37bdd 33bd4
  //   3fbca
endmodule

module _18_Bit_ALU (
  input  [17:0] Input1,
  input  [17:0] Input2,
  input  [1:0] Operation,
  output Carry_Out,
  output [17:0] Result
);

  wire [17:0] and_1_out, n18_bit_adder_1_inst_read, or_1_out, xor_1_out;

  assign and_1_out = Input1 & Input2;  // AND_Gate and_1, 18 bits wide
  _18_bit_adder u_18_bit_adder_1 (.INST_Read(n18_bit_adder_1_inst_read), .c_out(Carry_Out), .A(Input1), .B(Input2));
  assign or_1_out = Input1 | Input2;  // OR_Gate or_1, 18 bits wide
  assign xor_1_out = Input1 ^ Input2;  // XOR_Gate xor_1, 18 bits wide
  Multiplexer #(.select(2), .width(18)) multiplexer_1 (
    .in0(and_1_out), .in1(n18_bit_adder_1_inst_read), .in2(or_1_out), .in3(xor_1_out), .out(Result),
    .sel(Operation));  // open: en
endmodule

module Half_Adder (
  input  A,
  input  B,
  output Sum,
  output Carry_Out
);

  xor xor_1 (Sum, A, B);
  and and_1 (Carry_Out, A, B);
endmodule

module Full_Adder (
  input  A,
  input  B,
  input  Carry_In,
  output Sum,
  output Carry_Out
);

  wire and_1_out, and_2_out, xor_1_out;

  xor xor_1 (xor_1_out, A, B);
  and and_1 (and_1_out, A, B);
  xor xor_2 (Sum, xor_1_out, Carry_In);
  and and_2 (and_2_out, Carry_In, xor_1_out);
  or or_1 (Carry_Out, and_2_out, and_1_out);
endmodule

module Half_Comparator (
  input  A,
  input  B,
  output LT,
  output EQ,
  output GT
);

  wire not_1_out, not_2_out;

  not not_1 (not_1_out, A);
  not not_2 (not_2_out, B);
  and and_1 (LT, not_1_out, B);
  and and_2 (GT, A, not_2_out);
  xnor xnor_1 (EQ, B, A);
endmodule

module Full_Comparator (
  input  A,
  input  B,
  input  EQ_IN,
  input  GT_IN,
  input  LT_IN,
  output EQ_OUT,
  output GT_OUT,
  output LT_OUT
);

  wire and_1_out, and_2_out, not_1_out, not_2_out, xnor_1_out;

  not not_1 (not_1_out, B);
  not not_2 (not_2_out, A);
  xnor xnor_1 (xnor_1_out, A, B);
  and and_1 (and_1_out, A, not_1_out, EQ_IN);
  and and_2 (and_2_out, not_2_out, B, EQ_IN);
  and and_3 (EQ_OUT, xnor_1_out, EQ_IN);
  or or_1 (GT_OUT, and_1_out, GT_IN);
  or or_2 (LT_OUT, and_2_out, LT_IN);
endmodule

// adder
module _18_bit_adder (
  input  [17:0] A,
  input  [17:0] B,
  output [17:0] INST_Read,
  output c_out
);

  wire full_adder_1_carry_out, full_adder_2_carry_out, full_adder_3_carry_out, full_adder_4_carry_out,
       full_adder_5_carry_out, full_adder_6_carry_out, full_adder_7_carry_out, full_adder_8_carry_out,
       full_adder_9_carry_out, full_adder_10_carry_out, full_adder_11_carry_out, full_adder_12_carry_out,
       full_adder_13_carry_out, full_adder_14_carry_out, full_adder_15_carry_out, full_adder_16_carry_out,
       half_adder_1_carry_out;

  Half_Adder half_adder_1 (.B(A[0]), .Sum(INST_Read[0]), .Carry_Out(half_adder_1_carry_out), .A(B[0]));
  Full_Adder full_adder_1 (
    .A(A[1]), .B(B[1]), .Carry_In(half_adder_1_carry_out), .Sum(INST_Read[1]),
    .Carry_Out(full_adder_1_carry_out));
  Full_Adder full_adder_2 (
    .A(A[2]), .B(B[2]), .Carry_In(full_adder_1_carry_out), .Sum(INST_Read[2]),
    .Carry_Out(full_adder_2_carry_out));
  Full_Adder full_adder_3 (
    .A(A[3]), .B(B[3]), .Carry_In(full_adder_2_carry_out), .Sum(INST_Read[3]),
    .Carry_Out(full_adder_3_carry_out));
  Full_Adder full_adder_4 (
    .A(A[4]), .B(B[4]), .Carry_In(full_adder_3_carry_out), .Sum(INST_Read[4]),
    .Carry_Out(full_adder_4_carry_out));
  Full_Adder full_adder_5 (
    .A(A[5]), .B(B[5]), .Carry_In(full_adder_4_carry_out), .Sum(INST_Read[5]),
    .Carry_Out(full_adder_5_carry_out));
  Full_Adder full_adder_6 (
    .A(A[6]), .B(B[6]), .Carry_In(full_adder_5_carry_out), .Sum(INST_Read[6]),
    .Carry_Out(full_adder_6_carry_out));
  Full_Adder full_adder_7 (
    .A(A[7]), .B(B[7]), .Carry_In(full_adder_6_carry_out), .Sum(INST_Read[7]),
    .Carry_Out(full_adder_7_carry_out));
  Full_Adder full_adder_8 (
    .A(A[8]), .B(B[8]), .Carry_In(full_adder_7_carry_out), .Sum(INST_Read[8]),
    .Carry_Out(full_adder_8_carry_out));
  Full_Adder full_adder_9 (
    .A(A[9]), .B(B[9]), .Carry_In(full_adder_8_carry_out), .Sum(INST_Read[9]),
    .Carry_Out(full_adder_9_carry_out));
  Full_Adder full_adder_10 (
    .A(A[10]), .B(B[10]), .Carry_In(full_adder_9_carry_out), .Sum(INST_Read[10]),
    .Carry_Out(full_adder_10_carry_out));
  Full_Adder full_adder_11 (
    .A(A[11]), .B(B[11]), .Carry_In(full_adder_10_carry_out), .Sum(INST_Read[11]),
    .Carry_Out(full_adder_11_carry_out));
  Full_Adder full_adder_12 (
    .A(A[12]), .B(B[12]), .Carry_In(full_adder_11_carry_out), .Sum(INST_Read[12]),
    .Carry_Out(full_adder_12_carry_out));
  Full_Adder full_adder_13 (
    .A(A[13]), .B(B[13]), .Carry_In(full_adder_12_carry_out), .Sum(INST_Read[13]),
    .Carry_Out(full_adder_13_carry_out));
  Full_Adder full_adder_14 (
    .A(A[14]), .B(B[14]), .Carry_In(full_adder_13_carry_out), .Sum(INST_Read[14]),
    .Carry_Out(full_adder_14_carry_out));
  Full_Adder full_adder_15 (
    .A(A[15]), .B(B[15]), .Carry_In(full_adder_14_carry_out), .Sum(INST_Read[15]),
    .Carry_Out(full_adder_15_carry_out));
  Full_Adder full_adder_16 (
    .A(A[16]), .B(B[16]), .Carry_In(full_adder_15_carry_out), .Sum(INST_Read[16]),
    .Carry_Out(full_adder_16_carry_out));
  Full_Adder full_adder_17 (
    .A(A[17]), .B(B[17]), .Carry_In(full_adder_16_carry_out), .Sum(INST_Read[17]), .Carry_Out(c_out));
endmodule

module _18_Bit_Comparator (
  input  [17:0] A,
  input  [17:0] B,
  output EQ,
  output GT,
  output LT
);

  wire full_comparator_1_eq_out, full_comparator_1_gt_out, full_comparator_1_lt_out,
       full_comparator_2_eq_out, full_comparator_2_gt_out, full_comparator_2_lt_out,
       full_comparator_3_eq_out, full_comparator_3_gt_out, full_comparator_3_lt_out,
       full_comparator_4_eq_out, full_comparator_4_gt_out, full_comparator_4_lt_out,
       full_comparator_5_eq_out, full_comparator_5_gt_out, full_comparator_5_lt_out,
       full_comparator_6_eq_out, full_comparator_6_gt_out, full_comparator_6_lt_out,
       full_comparator_7_eq_out, full_comparator_7_gt_out, full_comparator_7_lt_out,
       full_comparator_8_eq_out, full_comparator_8_gt_out, full_comparator_8_lt_out,
       full_comparator_9_eq_out, full_comparator_9_gt_out, full_comparator_9_lt_out,
       full_comparator_10_eq_out, full_comparator_10_gt_out, full_comparator_10_lt_out,
       full_comparator_11_eq_out, full_comparator_11_gt_out, full_comparator_11_lt_out,
       full_comparator_12_eq_out, full_comparator_12_gt_out, full_comparator_12_lt_out,
       full_comparator_13_eq_out, full_comparator_13_gt_out, full_comparator_13_lt_out,
       full_comparator_14_eq_out, full_comparator_14_gt_out, full_comparator_14_lt_out,
       full_comparator_15_eq_out, full_comparator_15_gt_out, full_comparator_15_lt_out,
       full_comparator_16_eq_out, full_comparator_16_gt_out, full_comparator_16_lt_out, half_comparator_1_eq,
       half_comparator_1_gt, half_comparator_1_lt;

  Half_Comparator half_comparator_1 (
    .A(A[0]), .B(B[0]), .LT(half_comparator_1_lt), .EQ(half_comparator_1_eq), .GT(half_comparator_1_gt));
  Full_Comparator full_comparator_1 (
    .A(A[1]), .B(B[1]), .EQ_IN(half_comparator_1_eq), .GT_IN(half_comparator_1_gt),
    .LT_IN(half_comparator_1_lt), .EQ_OUT(full_comparator_1_eq_out), .GT_OUT(full_comparator_1_gt_out),
    .LT_OUT(full_comparator_1_lt_out));
  Full_Comparator full_comparator_2 (
    .A(A[2]), .B(B[2]), .EQ_IN(full_comparator_1_eq_out), .GT_IN(full_comparator_1_gt_out),
    .LT_IN(full_comparator_1_lt_out), .EQ_OUT(full_comparator_2_eq_out), .GT_OUT(full_comparator_2_gt_out),
    .LT_OUT(full_comparator_2_lt_out));
  Full_Comparator full_comparator_3 (
    .A(A[3]), .B(B[3]), .EQ_IN(full_comparator_2_eq_out), .GT_IN(full_comparator_2_gt_out),
    .LT_IN(full_comparator_2_lt_out), .EQ_OUT(full_comparator_3_eq_out), .GT_OUT(full_comparator_3_gt_out),
    .LT_OUT(full_comparator_3_lt_out));
  Full_Comparator full_comparator_4 (
    .A(A[4]), .B(B[4]), .EQ_IN(full_comparator_3_eq_out), .GT_IN(full_comparator_3_gt_out),
    .LT_IN(full_comparator_3_lt_out), .EQ_OUT(full_comparator_4_eq_out), .GT_OUT(full_comparator_4_gt_out),
    .LT_OUT(full_comparator_4_lt_out));
  Full_Comparator full_comparator_5 (
    .A(A[5]), .B(B[5]), .EQ_IN(full_comparator_4_eq_out), .GT_IN(full_comparator_4_gt_out),
    .LT_IN(full_comparator_4_lt_out), .EQ_OUT(full_comparator_5_eq_out), .GT_OUT(full_comparator_5_gt_out),
    .LT_OUT(full_comparator_5_lt_out));
  Full_Comparator full_comparator_6 (
    .A(A[6]), .B(B[6]), .EQ_IN(full_comparator_5_eq_out), .GT_IN(full_comparator_5_gt_out),
    .LT_IN(full_comparator_5_lt_out), .EQ_OUT(full_comparator_6_eq_out), .GT_OUT(full_comparator_6_gt_out),
    .LT_OUT(full_comparator_6_lt_out));
  Full_Comparator full_comparator_7 (
    .A(A[7]), .B(B[7]), .EQ_IN(full_comparator_6_eq_out), .GT_IN(full_comparator_6_gt_out),
    .LT_IN(full_comparator_6_lt_out), .EQ_OUT(full_comparator_7_eq_out), .GT_OUT(full_comparator_7_gt_out),
    .LT_OUT(full_comparator_7_lt_out));
  Full_Comparator full_comparator_8 (
    .A(A[8]), .B(B[8]), .EQ_IN(full_comparator_7_eq_out), .GT_IN(full_comparator_7_gt_out),
    .LT_IN(full_comparator_7_lt_out), .EQ_OUT(full_comparator_8_eq_out), .GT_OUT(full_comparator_8_gt_out),
    .LT_OUT(full_comparator_8_lt_out));
  Full_Comparator full_comparator_9 (
    .A(A[9]), .B(B[9]), .EQ_IN(full_comparator_8_eq_out), .GT_IN(full_comparator_8_gt_out),
    .LT_IN(full_comparator_8_lt_out), .EQ_OUT(full_comparator_9_eq_out), .GT_OUT(full_comparator_9_gt_out),
    .LT_OUT(full_comparator_9_lt_out));
  Full_Comparator full_comparator_10 (
    .A(A[10]), .B(B[10]), .EQ_IN(full_comparator_9_eq_out), .GT_IN(full_comparator_9_gt_out),
    .LT_IN(full_comparator_9_lt_out), .EQ_OUT(full_comparator_10_eq_out), .GT_OUT(full_comparator_10_gt_out),
    .LT_OUT(full_comparator_10_lt_out));
  Full_Comparator full_comparator_11 (
    .A(A[11]), .B(B[11]), .EQ_IN(full_comparator_10_eq_out), .GT_IN(full_comparator_10_gt_out),
    .LT_IN(full_comparator_10_lt_out), .EQ_OUT(full_comparator_11_eq_out),
    .GT_OUT(full_comparator_11_gt_out), .LT_OUT(full_comparator_11_lt_out));
  Full_Comparator full_comparator_12 (
    .A(A[12]), .B(B[12]), .EQ_IN(full_comparator_11_eq_out), .GT_IN(full_comparator_11_gt_out),
    .LT_IN(full_comparator_11_lt_out), .EQ_OUT(full_comparator_12_eq_out),
    .GT_OUT(full_comparator_12_gt_out), .LT_OUT(full_comparator_12_lt_out));
  Full_Comparator full_comparator_13 (
    .A(A[13]), .B(B[13]), .EQ_IN(full_comparator_12_eq_out), .GT_IN(full_comparator_12_gt_out),
    .LT_IN(full_comparator_12_lt_out), .EQ_OUT(full_comparator_13_eq_out),
    .GT_OUT(full_comparator_13_gt_out), .LT_OUT(full_comparator_13_lt_out));
  Full_Comparator full_comparator_14 (
    .A(A[14]), .B(B[14]), .EQ_IN(full_comparator_13_eq_out), .GT_IN(full_comparator_13_gt_out),
    .LT_IN(full_comparator_13_lt_out), .EQ_OUT(full_comparator_14_eq_out),
    .GT_OUT(full_comparator_14_gt_out), .LT_OUT(full_comparator_14_lt_out));
  Full_Comparator full_comparator_15 (
    .A(A[15]), .B(B[15]), .EQ_IN(full_comparator_14_eq_out), .GT_IN(full_comparator_14_gt_out),
    .LT_IN(full_comparator_14_lt_out), .EQ_OUT(full_comparator_15_eq_out),
    .GT_OUT(full_comparator_15_gt_out), .LT_OUT(full_comparator_15_lt_out));
  Full_Comparator full_comparator_16 (
    .A(A[16]), .B(B[16]), .EQ_IN(full_comparator_15_eq_out), .GT_IN(full_comparator_15_gt_out),
    .LT_IN(full_comparator_15_lt_out), .EQ_OUT(full_comparator_16_eq_out),
    .GT_OUT(full_comparator_16_gt_out), .LT_OUT(full_comparator_16_lt_out));
  Full_Comparator full_comparator_17 (
    .A(A[17]), .B(B[17]), .EQ_IN(full_comparator_16_eq_out), .GT_IN(full_comparator_16_gt_out),
    .LT_IN(full_comparator_16_lt_out), .EQ_OUT(EQ), .GT_OUT(GT), .LT_OUT(LT));
endmodule

module _14_Bit_Adder (
  input  [13:0] A,
  input  [13:0] B,
  output [13:0] INST_Read,
  output c_out
);

  wire full_adder_1_carry_out, full_adder_2_carry_out, full_adder_3_carry_out, full_adder_4_carry_out,
       full_adder_5_carry_out, full_adder_6_carry_out, full_adder_7_carry_out, full_adder_8_carry_out,
       full_adder_9_carry_out, full_adder_10_carry_out, full_adder_11_carry_out, full_adder_12_carry_out,
       half_adder_1_carry_out;

  Half_Adder half_adder_1 (.B(A[0]), .Sum(INST_Read[0]), .Carry_Out(half_adder_1_carry_out), .A(B[0]));
  Full_Adder full_adder_1 (
    .A(A[1]), .B(B[1]), .Carry_In(half_adder_1_carry_out), .Sum(INST_Read[1]),
    .Carry_Out(full_adder_1_carry_out));
  Full_Adder full_adder_2 (
    .A(A[2]), .B(B[2]), .Carry_In(full_adder_1_carry_out), .Sum(INST_Read[2]),
    .Carry_Out(full_adder_2_carry_out));
  Full_Adder full_adder_3 (
    .A(A[3]), .B(B[3]), .Carry_In(full_adder_2_carry_out), .Sum(INST_Read[3]),
    .Carry_Out(full_adder_3_carry_out));
  Full_Adder full_adder_4 (
    .A(A[4]), .B(B[4]), .Carry_In(full_adder_3_carry_out), .Sum(INST_Read[4]),
    .Carry_Out(full_adder_4_carry_out));
  Full_Adder full_adder_5 (
    .A(A[5]), .B(B[5]), .Carry_In(full_adder_4_carry_out), .Sum(INST_Read[5]),
    .Carry_Out(full_adder_5_carry_out));
  Full_Adder full_adder_6 (
    .A(A[6]), .B(B[6]), .Carry_In(full_adder_5_carry_out), .Sum(INST_Read[6]),
    .Carry_Out(full_adder_6_carry_out));
  Full_Adder full_adder_7 (
    .A(A[7]), .B(B[7]), .Carry_In(full_adder_6_carry_out), .Sum(INST_Read[7]),
    .Carry_Out(full_adder_7_carry_out));
  Full_Adder full_adder_8 (
    .A(A[8]), .B(B[8]), .Carry_In(full_adder_7_carry_out), .Sum(INST_Read[8]),
    .Carry_Out(full_adder_8_carry_out));
  Full_Adder full_adder_9 (
    .A(A[9]), .B(B[9]), .Carry_In(full_adder_8_carry_out), .Sum(INST_Read[9]),
    .Carry_Out(full_adder_9_carry_out));
  Full_Adder full_adder_10 (
    .A(A[10]), .B(B[10]), .Carry_In(full_adder_9_carry_out), .Sum(INST_Read[10]),
    .Carry_Out(full_adder_10_carry_out));
  Full_Adder full_adder_11 (
    .A(A[11]), .B(B[11]), .Carry_In(full_adder_10_carry_out), .Sum(INST_Read[11]),
    .Carry_Out(full_adder_11_carry_out));
  Full_Adder full_adder_12 (
    .A(A[12]), .B(B[12]), .Carry_In(full_adder_11_carry_out), .Sum(INST_Read[12]),
    .Carry_Out(full_adder_12_carry_out));
  Full_Adder full_adder_13 (
    .A(A[13]), .B(B[13]), .Carry_In(full_adder_12_carry_out), .Sum(INST_Read[13]), .Carry_Out(c_out));
endmodule
